# Fritzing sketch hw-sketch (saved by Fritzing 0.9.3b)
circuit board: 9.04684cm x 6.14852cm
breadboards: 1

parts:
  Q1 = NPN-Transistor [package="TO92 [THT]"]
  LED1 = LED - 5mm [color="Infrared (940nm)" current=100mA package="5 mm [THT]"]
  R1 = Resistor [tolerance=±20% resistance=1k package=THT]
  R2 = Resistor [tolerance=±5% resistance=47 package=THT]
  WeMos_D1_Mini1 = WeMos D1 Mini
  DHT22_/_AM2303 = Humidity and Temperature Sensor RHT03
  R3 = Resistor [tolerance=±5% resistance=150 package=THT]
  R5 = Resistor [tolerance=±5% resistance=100 package=THT]
  R4 = Resistor [tolerance=±1% resistance=100 package=THT]
  LED2 = RGB LED (com. cathode, rbg) [package="5 mm [THT]"]  # not connected

nets:
  N1: Q1.E, WeMos_D1_Mini1.G, DHT22_/_AM2303.GND_2
  N2: Q1.B, R1.Pin_0
  N3: Q1.C, LED1.cathode
  N4: LED1.anode, R2.Pin_0
  N5: R1.Pin_1, WeMos_D1_Mini1.D2
  N6: R2.Pin_1, WeMos_D1_Mini1.5V
  3V3: WeMos_D1_Mini1.3V3, DHT22_/_AM2303.Vcc
  N7: WeMos_D1_Mini1.D0, DHT22_/_AM2303.Data-signal
  N8: WeMos_D1_Mini1.D1, R4.Pin_1
  N9: WeMos_D1_Mini1.D3, R3.Pin_1
  N10: WeMos_D1_Mini1.D8, R5.Pin_1

notes:
  D1 Mini
  D5: CLK (Clock)
  D6: MISO
  D7: MOSI
  D4: CS
